# Fritzing sketch rstft (saved by Fritzing 0.9.3b)

parts:
  ZS-042_RTC1 = ZS-042 RTC Module  # not connected
  J1 = female pin header, 6 pins [form="♀ (female)"]
  R1 = Photocell (LDR) [package=THT]
  R2 = Temperature Sensor (Thermistor) [thermistor_type=NTC package=THT]
  R3 = Resistor [tolerance=±5% resistance=10k package=THT]
  R4 = Resistor [tolerance=±5% resistance=57k package=THT]
  Part1 = Arduino Prototyping Shield

nets:
  N1: J1.pin1, Part1.N$135
  N2: J1.pin2, Part1.SCL, Part1.N$132
  N3: J1.pin3, Part1.SDA, Part1.N$120
  N4: J1.pin4, R2.pin_1, R3.Pin_1, Part1.+5V, Part1.N$107, Part1.N$238, Part1.N$396
  N5: J1.pin5, R1.pin_0, R4.Pin_1, Part1.GND, Part1.N$95, Part1.N$117, Part1.N$282
  N6: J1.pin6, Part1.N$83
  N7: R1.pin_1, R3.Pin_0, Part1.A4, Part1.N$323, Part1.N$411
  N8: R2.pin_0, R4.Pin_0, Part1.A5, Part1.N$318, Part1.N$403
